// Logisim project computer.circ as structural Verilog: 10 circuits, main circuit main
module main (
);

  wire and_2_out, and_3_out, and_4_out, and_5_out, and_6_out, and_7_out, and_8_out, button_1_out, clock,
       clock_1_out, comparator_1_eq, comparator_2_gt, comparator_3_eq, CONTINUE_out, cpu_1_hlt, cpu_1_load,
       eq16_1_out_3, eq16_2_out_3, eq16_3_out_3, eq16_4_out_3, eq16_5_out_3, keyboard_1_avail, or_1_out,
       or_2_out, or_3_out, rst;
  wire [6:0] keyboard_1_data;
  wire [7:0] cpu_1_address, cpu_1_address_2;
  wire [15:0] cpu_1_data_out, videomem_1_data_out, videomem_1_out0, videomem_1_out1, videomem_1_out2,
       videomem_1_out3, videomem_1_out4, videomem_1_out5, videomem_1_out6, videomem_1_out7, videomem_1_out8,
       videomem_1_out9, videomem_1_outa, videomem_1_outb, videomem_1_outc, videomem_1_outd, videomem_1_oute,
       videomem_1_outf;

  Button CONTINUE (.out(CONTINUE_out));
  Button RESET (.out(rst));
  Clock clock_1 (.out(clock_1_out));
  or or_1 (or_1_out, clock_1_out, button_1_out);
  Button button_1 (.out(button_1_out));
  TTY tty_1 (.data(cpu_1_data_out[6:0]), .clk(clock), .we(and_2_out), .clr(or_2_out));
  or or_2 (or_2_out, rst, and_3_out);
  Keyboard keyboard_1 (.clk(clock), .re(and_4_out), .clr(rst), .avail(keyboard_1_avail), .data(keyboard_1_data));
  and and_1 (clock, ~cpu_1_hlt, or_1_out);  // AND_Gate
  CPU cpu_1 (
    .Address({cpu_1_address_2, cpu_1_address}), .reset(rst), .clock(clock), .Data_in(cpu_1_data_out),
    .load(cpu_1_load), .Data_out(cpu_1_data_out), .HLT(cpu_1_hlt), .continue__cancels_halt(CONTINUE_out));
  and and_2 (and_2_out, ~cpu_1_load, eq16_1_out_3);  // AND_Gate
  and and_3 (and_3_out, ~cpu_1_load, eq16_2_out_3);  // AND_Gate
  and and_4 (and_4_out, cpu_1_load, eq16_3_out_3);
  assign cpu_1_data_out[6:0] = and_4_out ? keyboard_1_data : 7'bz;  // Controlled_Buffer controlled_buffer_1
  and and_5 (and_5_out, cpu_1_load, eq16_4_out_3);
  assign cpu_1_data_out[0] = and_5_out ? keyboard_1_avail : 1'bz;  // Controlled_Buffer controlled_buffer_2
  Comparator comparator_1 (.a(cpu_1_address_2), .b({8{1'b0}}), .eq(comparator_1_eq));  // open: gt, lt
  eq16 eq16_1 (.A(16'h111), .B({cpu_1_address_2, cpu_1_address}), .out_3(eq16_1_out_3));
  eq16 eq16_2 (.A(16'h112), .B({cpu_1_address_2, cpu_1_address}), .out_3(eq16_2_out_3));
  eq16 eq16_3 (.A(16'h113), .B({cpu_1_address_2, cpu_1_address}), .out_3(eq16_3_out_3));
  eq16 eq16_4 (.A(16'h114), .B({cpu_1_address_2, cpu_1_address}), .out_3(eq16_4_out_3));
  Comparator #(.width(16), .mode("unsigned")) comparator_2 (
    .a({cpu_1_address_2, cpu_1_address}), .b(16'h1ff), .gt(comparator_2_gt));  // open: eq, lt
  Pull_Resistor pull_resistor_1 (.node(cpu_1_data_out));
  ROM #(.dataWidth(16)) rom_1 (.addr(cpu_1_address), .data(cpu_1_data_out), .sel(comparator_1_eq));
  RAM #(.addrWidth(16), .dataWidth(16)) ram_1 (
    .addr({cpu_1_address_2, cpu_1_address}), .data(cpu_1_data_out), .sel(comparator_2_gt), .clk(clock),
    .ld(cpu_1_load));  // open: clr
  DotMatrix #(.matrixcols(16), .matrixrows(16)) dotmatrix_1 (
    .col0(videomem_1_out0), .col1(videomem_1_out1), .col2(videomem_1_out2), .col3(videomem_1_out3),
    .col4(videomem_1_out4), .col5(videomem_1_out5), .col6(videomem_1_out6), .col7(videomem_1_out7),
    .col8(videomem_1_out8), .col9(videomem_1_out9), .col10(videomem_1_outa), .col11(videomem_1_outb),
    .col12(videomem_1_outc), .col13(videomem_1_outd), .col14(videomem_1_oute), .col15(videomem_1_outf));
  or or_3 (or_3_out, rst, and_6_out);
  and and_6 (and_6_out, eq16_5_out_3, ~cpu_1_load);  // AND_Gate
  eq16 eq16_5 (.A({cpu_1_address_2, cpu_1_address}), .B(16'h110), .out_3(eq16_5_out_3));
  Hex_Digit_Display hex_digit_display_1 (.value(cpu_1_address_2[7:4]));  // open: dp
  and and_7 (and_7_out, ~cpu_1_load, comparator_3_eq);  // AND_Gate
  Comparator #(.width(12)) comparator_3 (
    .a({cpu_1_address_2, cpu_1_address[7:4]}), .b(12'h10), .eq(comparator_3_eq));  // open: gt, lt
  and and_8 (and_8_out, comparator_3_eq, cpu_1_load);
  Hex_Digit_Display hex_digit_display_2 (.value(cpu_1_address[7:4]));  // open: dp
  Hex_Digit_Display hex_digit_display_3 (.value(cpu_1_address_2[3:0]));  // open: dp
  videomem videomem_1 (
    .clock(clock), .rst(or_3_out), .out0(videomem_1_out0), .out1(videomem_1_out1), .out2(videomem_1_out2),
    .out3(videomem_1_out3), .out4(videomem_1_out4), .out5(videomem_1_out5), .out6(videomem_1_out6),
    .out7(videomem_1_out7), .out8(videomem_1_out8), .out9(videomem_1_out9), .outA(videomem_1_outa),
    .outB(videomem_1_outb), .outC(videomem_1_outc), .outD(videomem_1_outd), .outE(videomem_1_oute),
    .outF(videomem_1_outf), .adr(cpu_1_address[3:0]), .write(and_7_out), .data_out(videomem_1_data_out),
    .data_in(cpu_1_data_out));
  assign cpu_1_data_out = and_8_out ? videomem_1_data_out : 16'bz;  // Controlled_Buffer controlled_buffer_3
  Hex_Digit_Display hex_digit_display_4 (.value(cpu_1_address[3:0]));  // open: dp
  Hex_Digit_Display hex_digit_display_5 (.value(cpu_1_data_out[11:8]));  // open: dp
  Hex_Digit_Display hex_digit_display_6 (.value(cpu_1_data_out[15:12]));  // open: dp
  Hex_Digit_Display hex_digit_display_7 (.value(cpu_1_data_out[3:0]));  // open: dp
  Hex_Digit_Display hex_digit_display_8 (.value(cpu_1_data_out[7:4]));  // open: dp

  // Notes on the sheet:
  //   ROM
  //   RAM
  //   contents of rom_1 (hex, n*v repeats v):
  //   11c0 e000 1400 112 1000 48 1400 111 1000 69 1400 111 1000 2c 1400 111 1000 20 1400 111 1000 49 1400
  //   111 1000 27 1400 111 1000 6d 1400 111 1000 20 1400 111 1000 5a 1400 111 1000 61 1400 111 1000 63
  //   1400 111 1000 6b 1400 111 1000 21 1400 111 1000 a 1400 111 1400 110 1000 60 1400 101 1400 10e 1000
  //   1878 1400 102 1400 10d 1000 3c7c 1400 103 1400 104 1400 10b 1400 10c 1000 187e 1400 105 1400 10a
  //   1000 7e 1400 106 1400 107 1400 108 1400 109 1200 200 3c49 3e01 c200 80 d000 1400 111 f200 3042 22c0
  //   1403 111 4000 3e01 c400 6f f200 3c49 1200 114 3e01 c200 78 1200 113 f200 200 c000 80 1400 112 f200
  //   1400 110 f200 1040 f 3491 1040 100 3091 2413 f200 22c0 1403 100 4000 22c0 1403 101 4000 22c0 1403
  //   102 4000 22c0 1403 103 4000 22c0 1403 104 4000 22c0 1403 105 4000 22c0 1403 106 4000 22c0 1403 107
  //   4000 22c0 1403 108 4000 22c0 1403 109 4000 22c0 1403 10a 4000 22c0 1403 10b 4000 22c0 1403 10c 4000
  //   22c0 1403 10d 4000 22c0 1403 10e 4000 22c0 1403 10f f200
  //   ADDRESS
  //   DATA
endmodule

module videomem (
  input  [15:0] data_in,
  input  write,
  input  [3:0] adr,
  input  clock,
  input  rst,
  output [15:0] out0,
  output [15:0] out1,
  output [15:0] out2,
  output [15:0] out3,
  output [15:0] out4,
  output [15:0] out5,
  output [15:0] out6,
  output [15:0] out7,
  output [15:0] out8,
  output [15:0] out9,
  output [15:0] outA,
  output [15:0] outB,
  output [15:0] outC,
  output [15:0] outD,
  output [15:0] outE,
  output [15:0] outF,
  output [15:0] data_out
);

  wire demultiplexer_1_out0, demultiplexer_1_out1, demultiplexer_1_out2, demultiplexer_1_out3,
       demultiplexer_1_out4, demultiplexer_1_out5, demultiplexer_1_out6, demultiplexer_1_out7,
       demultiplexer_1_out8, demultiplexer_1_out9, demultiplexer_1_out10, demultiplexer_1_out11,
       demultiplexer_1_out12, demultiplexer_1_out13, demultiplexer_1_out14, demultiplexer_1_out15;

  Demultiplexer #(.select(4), .enable("false")) demultiplexer_1 (
    .out0(demultiplexer_1_out0), .out1(demultiplexer_1_out1), .out2(demultiplexer_1_out2),
    .out3(demultiplexer_1_out3), .out4(demultiplexer_1_out4), .out5(demultiplexer_1_out5),
    .out6(demultiplexer_1_out6), .out7(demultiplexer_1_out7), .out8(demultiplexer_1_out8),
    .out9(demultiplexer_1_out9), .out10(demultiplexer_1_out10), .out11(demultiplexer_1_out11),
    .out12(demultiplexer_1_out12), .out13(demultiplexer_1_out13), .out14(demultiplexer_1_out14),
    .out15(demultiplexer_1_out15), .in(write), .sel(adr));
  Register #(.width(16)) register_1 (.D(data_in), .en(demultiplexer_1_out0), .Q(out0), .clk(clock), .clr(rst));
  Register #(.width(16)) register_2 (.D(data_in), .en(demultiplexer_1_out2), .Q(out2), .clk(clock), .clr(rst));
  Register #(.width(16)) register_3 (.D(data_in), .en(demultiplexer_1_out4), .Q(out4), .clk(clock), .clr(rst));
  Register #(.width(16)) register_4 (.D(data_in), .en(demultiplexer_1_out6), .Q(out6), .clk(clock), .clr(rst));
  Register #(.width(16)) register_5 (.D(data_in), .en(demultiplexer_1_out8), .Q(out8), .clk(clock), .clr(rst));
  Register #(.width(16)) register_6 (.D(data_in), .en(demultiplexer_1_out10), .Q(outA), .clk(clock), .clr(rst));
  Register #(.width(16)) register_7 (.D(data_in), .en(demultiplexer_1_out12), .Q(outC), .clk(clock), .clr(rst));
  Register #(.width(16)) register_8 (.D(data_in), .en(demultiplexer_1_out14), .Q(outE), .clk(clock), .clr(rst));
  Register #(.width(16)) register_9 (.D(data_in), .en(demultiplexer_1_out1), .Q(out1), .clk(clock), .clr(rst));
  Register #(.width(16)) register_10 (.D(data_in), .en(demultiplexer_1_out3), .Q(out3), .clk(clock), .clr(rst));
  Register #(.width(16)) register_11 (.D(data_in), .en(demultiplexer_1_out5), .Q(out5), .clk(clock), .clr(rst));
  Register #(.width(16)) register_12 (.D(data_in), .en(demultiplexer_1_out7), .Q(out7), .clk(clock), .clr(rst));
  Register #(.width(16)) register_13 (.D(data_in), .en(demultiplexer_1_out9), .Q(out9), .clk(clock), .clr(rst));
  Register #(.width(16)) register_14 (.D(data_in), .en(demultiplexer_1_out11), .Q(outB), .clk(clock), .clr(rst));
  Register #(.width(16)) register_15 (.D(data_in), .en(demultiplexer_1_out13), .Q(outD), .clk(clock), .clr(rst));
  Register #(.width(16)) register_16 (.D(data_in), .en(demultiplexer_1_out15), .Q(outF), .clk(clock), .clr(rst));
  Multiplexer #(.select(4), .width(16), .enable("false")) multiplexer_1 (
    .in0(out0), .in1(out1), .in2(out2), .in3(out3), .in4(out4), .in5(out5), .in6(out6), .in7(out7),
    .in8(out8), .in9(out9), .in10(outA), .in11(outB), .in12(outC), .in13(outD), .in14(outE), .in15(outF),
    .out(data_out), .sel(adr));
endmodule

module CPU (
  input  reset,
  input  [15:0] Data_in,
  input  clock,
  input  continue__cancels_halt,
  output [15:0] Address,
  output load,
  output [15:0] Data_out,
  output HLT
);

  wire alu_1_c, alu_1_o, alu_1_s, alu_1_z_2, cin, datsel, decoder_1_hlt, decoder_1_rstphase, invY, loadim,
       loadir, memwr, or_1_out, or_2_out, pcload, regwr, XXen, Yen, ZZwr;
  wire [1:0] adrsel, counter_1_q, pcsel, regsel;
  wire [2:0] Xsel, Ysel, Zsel;
  wire [3:0] ALUop, flags_reg_1_q;
  wire [15:0] alu_1_z, alu_1_zz, Imm_q, incr16_1_out, IR_q, multiplexer_1_out, multiplexer_3_out,
       multiplexer_4_out, pc, regfile_1_x, regfile_1_xx, Ybus;

  not not_1 (load, memwr);
  assign Data_out = memwr ? multiplexer_1_out : 16'bz;  // Controlled_Buffer controlled_buffer_1
  Multiplexer #(.width(16), .enable("false")) multiplexer_1 (
    .in0(pc), .in1(Ybus), .out(multiplexer_1_out), .sel(datsel));
  Multiplexer #(.select(2), .width(16), .enable("false")) multiplexer_2 (
    .in0(pc), .in1(Imm_q), .in2(alu_1_z), .in3(Ybus), .out(Address), .sel(adrsel));
  Register #(.width(16)) IR (.D(Data_in), .en(loadir), .Q(IR_q), .clk(clock), .clr(reset));
  Counter #(.width(2), .max('h3)) counter_1 (
    .Q(counter_1_q), .clk(clock), .clr(or_1_out));  // open: load, D, count, carry
  or or_1 (or_1_out, reset, decoder_1_rstphase);
  Register #(.width(16)) Imm (.D(Data_in), .en(loadim), .Q(Imm_q), .clk(clock), .clr(reset));
  Multiplexer #(.select(2), .width(16), .enable("false")) multiplexer_3 (
    .in0(alu_1_z), .in1(Imm_q), .in2(incr16_1_out), .in3(Data_in), .out(multiplexer_3_out), .sel(pcsel));
  S_R_Flip_Flop #(.trigger("high")) s_r_ff_1 (
    .S(decoder_1_hlt), .clk(clock), .R(1'b0), .Q(HLT), .reset(or_2_out));  // open: Qn, preset, en
  or or_2 (or_2_out, continue__cancels_halt, reset);
  Register #(.width(16)) u_PC (.D(multiplexer_3_out), .en(pcload), .Q(pc), .clk(clock), .clr(reset));
  incr16 incr16_1 (.IN(pc), .OUT(incr16_1_out));  // open: carry
  Multiplexer #(.select(2), .width(16), .enable("false")) multiplexer_4 (
    .in0(Imm_q), .in1(Data_in), .in2(alu_1_z), .in3(Ybus), .out(multiplexer_4_out), .sel(regsel));
  decoder decoder_1 (
    .instr(IR_q), .phase(counter_1_q), .flags(flags_reg_1_q), .memwr(memwr), .regsel(regsel),
    .adrsel(adrsel), .loadir(loadir), .regwr(regwr), .datsel(datsel), .cin(cin), .loadim(loadim),
    .pcload(pcload), .invY(invY), .pcsel(pcsel), .Yenable(Yen), .Ysel(Ysel), .Zsel(Zsel), .Xsel(Xsel),
    .ALUop(ALUop), .HLT(decoder_1_hlt), .RSTPhase(decoder_1_rstphase), .XXen(XXen), .ZZwr(ZZwr));
  regfile regfile_1 (
    .XXen(XXen), .Xsel(Xsel), .Ysel(Ysel), .Z(multiplexer_4_out), .Zsel(Zsel), .ZZwr(ZZwr), .ZZ(alu_1_zz),
    .write(regwr), .XX(regfile_1_xx), .X(regfile_1_x), .Y(Ybus), .clock(clock), .reset(reset));
  ALU alu_1 (
    .invY(invY), .XX(regfile_1_xx), .Z(alu_1_z), .ZZ(alu_1_zz), .Y(Ybus), .X(regfile_1_x), .cin(cin),
    .instr(ALUop), .Y_enable(Yen), .Z_2(alu_1_z_2), .C(alu_1_c), .S(alu_1_s), .O(alu_1_o));
  flags_reg flags_reg_1 (
    .Z(alu_1_z_2), .C(alu_1_c), .S(alu_1_s), .O(alu_1_o), .clk(clock), .rst(reset), .Q(flags_reg_1_q));
  // Probe on flags_reg_1_q

  // Other names for the same wires on the sheet: rst = reset

  // Notes on the sheet:
  //   HALT
  //   Z / imm / ++ / data
endmodule

module regfile (
  input  XXen,
  input  [2:0] Xsel,
  input  [2:0] Ysel,
  input  write,
  input  [2:0] Zsel,
  input  ZZwr,
  input  [15:0] Z,
  input  [15:0] ZZ,
  input  clock,
  input  reset,
  output [15:0] XX,
  output [15:0] X,
  output [15:0] Y
);

  wire demultiplexer_1_out0, demultiplexer_1_out1, demultiplexer_1_out2, demultiplexer_1_out3,
       demultiplexer_1_out4, demultiplexer_1_out5, demultiplexer_1_out6, demultiplexer_1_out7, or_1_out;
  wire [15:0] multiplexer_1_out, register_1_q, register_2_q, register_3_q, register_4_q, register_5_q,
       register_6_q, register_7_q, register_8_q;

  Demultiplexer #(.select(3), .enable("false")) demultiplexer_1 (
    .out0(demultiplexer_1_out0), .out1(demultiplexer_1_out1), .out2(demultiplexer_1_out2),
    .out3(demultiplexer_1_out3), .out4(demultiplexer_1_out4), .out5(demultiplexer_1_out5),
    .out6(demultiplexer_1_out6), .out7(demultiplexer_1_out7), .in(write), .sel(Zsel));
  Multiplexer #(.width(16), .enable("false")) multiplexer_1 (.in0(Z), .in1(ZZ), .out(multiplexer_1_out), .sel(ZZwr));
  or or_1 (or_1_out, demultiplexer_1_out3, ZZwr);
  Register #(.width(16)) register_1 (.D(Z), .en(demultiplexer_1_out0), .Q(register_1_q), .clk(clock), .clr(reset));
  Register #(.width(16)) register_2 (.D(Z), .en(demultiplexer_1_out1), .Q(register_2_q), .clk(clock), .clr(reset));
  Register #(.width(16)) register_3 (.D(Z), .en(demultiplexer_1_out2), .Q(register_3_q), .clk(clock), .clr(reset));
  Register #(.width(16)) register_4 (.D(multiplexer_1_out), .en(or_1_out), .Q(register_4_q), .clk(clock), .clr(reset));
  Register #(.width(16)) register_5 (.D(Z), .en(demultiplexer_1_out4), .Q(register_5_q), .clk(clock), .clr(reset));
  Register #(.width(16)) register_6 (.D(Z), .en(demultiplexer_1_out5), .Q(register_6_q), .clk(clock), .clr(reset));
  Register #(.width(16)) register_7 (.D(Z), .en(demultiplexer_1_out6), .Q(register_7_q), .clk(clock), .clr(reset));
  Register #(.width(16)) register_8 (.D(Z), .en(demultiplexer_1_out7), .Q(register_8_q), .clk(clock), .clr(reset));
  assign XX = XXen ? register_4_q : 16'bz;  // Controlled_Buffer controlled_buffer_1
  Multiplexer #(.select(3), .width(16), .enable("false")) multiplexer_2 (
    .in0(register_1_q), .in1(register_2_q), .in2(register_3_q), .in3(register_4_q), .in4(register_5_q),
    .in5(register_6_q), .in6(register_7_q), .in7(register_8_q), .out(X), .sel(Xsel));
  Multiplexer #(.select(3), .width(16), .enable("false")) multiplexer_3 (
    .in0(register_1_q), .in1(register_2_q), .in2(register_3_q), .in3(register_4_q), .in4(register_5_q),
    .in5(register_6_q), .in6(register_7_q), .in7(register_8_q), .out(Y), .sel(Ysel));

  // Notes on the sheet:
  //   A
  //   B
  //   C
  //   D
  //   E
  //   F
  //   G
  //   SP
endmodule

module ALU (
  input  [15:0] Y,
  input  [15:0] X,
  input  Y_enable,
  input  invY,
  input  [3:0] instr,
  input  cin,
  input  [15:0] XX,
  output [15:0] Z,
  output Z_2,
  output S,
  output O,
  output C,
  output [15:0] ZZ
);

  wire adder_1_cout, \and , and_2_out, bitselector_1_out, bitselector_2_out, comparator_1_eq,
       comparator_2_eq, controlled_buffer_21_out, div, mul, \nand , nop, \nor , not_2_out, not_3_out, \or ,
       or_2_out, rol, ror, sar, shl, shr, tunnel, X_t, xnor_1_out, \xor , xor_3_out, Y_t;
  wire [3:0] bit_extender_2_out, not_1_out, subtractor_1_out;
  wire [15:0] adder_1_out, and_1_out, bit_extender_1_out, controlled_buffer_1_out, divider_1_out,
       divider_1_rem, multiplier_1_cout, multiplier_1_out, nand_1_out, nor_1_out, or_1_out, shifter_1_out,
       shifter_2_out, shifter_3_out, shifter_4_out, shifter_5_out, xor_1_out, xor_2_out;

  assign controlled_buffer_1_out = Y_enable ? Y : 16'bz;  // Controlled_Buffer controlled_buffer_1
  Pull_Resistor pull_resistor_1 (.node(controlled_buffer_1_out));
  assign bit_extender_1_out = {{15{invY}}, invY};  // Bit_Extender bit_extender_1
  assign xor_1_out = bit_extender_1_out ^ controlled_buffer_1_out;  // XOR_Gate xor_1, 16 bits wide
  Pull_Resistor pull_resistor_2 (.node(X));
  Bit_Extender #(.in_width(16), .out_width(4)) bit_extender_2 (.in(xor_1_out), .out(bit_extender_2_out));
  Adder #(.width(16)) adder_1 (.a(X), .b(xor_1_out), .out(adder_1_out), .cin(cin), .cout(adder_1_cout));
  Multiplier #(.width(16)) multiplier_1 (
    .a(X), .b(xor_1_out), .out(multiplier_1_out), .cin(XX), .cout(multiplier_1_cout));
  Divider #(.width(16)) divider_1 (.a(X), .b(xor_1_out), .out(divider_1_out), .upper(XX), .rem(divider_1_rem));
  assign and_1_out = X & xor_1_out;  // AND_Gate and_1, 16 bits wide
  assign or_1_out = X | xor_1_out;  // OR_Gate or_1, 16 bits wide
  assign nand_1_out = ~(X & xor_1_out);  // NAND_Gate nand_1, 16 bits wide
  assign nor_1_out = ~(X | xor_1_out);  // NOR_Gate nor_1, 16 bits wide
  assign xor_2_out = X ^ xor_1_out;  // XOR_Gate xor_2, 16 bits wide
  Shifter #(.width(16)) shifter_1 (.in(X), .\dist (bit_extender_2_out), .out(shifter_1_out));
  Shifter #(.width(16), .shift("lr")) shifter_2 (.in(X), .\dist (bit_extender_2_out), .out(shifter_2_out));
  Shifter #(.width(16), .shift("ar")) shifter_3 (.in(X), .\dist (bit_extender_2_out), .out(shifter_3_out));
  Shifter #(.width(16), .shift("rl")) shifter_4 (.in(X), .\dist (bit_extender_2_out), .out(shifter_4_out));
  Shifter #(.width(16), .shift("rr")) shifter_5 (.in(X), .\dist (bit_extender_2_out), .out(shifter_5_out));
  assign Z = X_t ? X : 16'bz;  // Controlled_Buffer controlled_buffer_2
  assign Z = Y_t ? xor_1_out : 16'bz;  // Controlled_Buffer controlled_buffer_3
  assign Z = tunnel ? adder_1_out : 16'bz;  // Controlled_Buffer controlled_buffer_4
  assign C = tunnel ? adder_1_cout : 1'bz;  // Controlled_Buffer controlled_buffer_5
  assign Z = mul ? multiplier_1_out : 16'bz;  // Controlled_Buffer controlled_buffer_6
  assign ZZ = mul ? multiplier_1_cout : 16'bz;  // Controlled_Buffer controlled_buffer_7
  assign Z = div ? divider_1_out : 16'bz;  // Controlled_Buffer controlled_buffer_8
  assign ZZ = div ? divider_1_rem : 16'bz;  // Controlled_Buffer controlled_buffer_9
  assign Z = \and  ? and_1_out : 16'bz;  // Controlled_Buffer controlled_buffer_10
  assign Z = \or  ? or_1_out : 16'bz;  // Controlled_Buffer controlled_buffer_11
  assign Z = \nand  ? nand_1_out : 16'bz;  // Controlled_Buffer controlled_buffer_12
  assign Z = \nor  ? nor_1_out : 16'bz;  // Controlled_Buffer controlled_buffer_13
  assign Z = \xor  ? xor_2_out : 16'bz;  // Controlled_Buffer controlled_buffer_14
  assign Z = shl ? shifter_1_out : 16'bz;  // Controlled_Buffer controlled_buffer_15
  assign Z = shr ? shifter_2_out : 16'bz;  // Controlled_Buffer controlled_buffer_16
  assign Z = sar ? shifter_3_out : 16'bz;  // Controlled_Buffer controlled_buffer_17
  assign Z = rol ? shifter_4_out : 16'bz;  // Controlled_Buffer controlled_buffer_18
  assign Z = ror ? shifter_5_out : 16'bz;  // Controlled_Buffer controlled_buffer_19
  Pull_Resistor pull_resistor_3 (.node(Z));
  assign not_1_out = ~bit_extender_2_out;  // NOT_Gate not_1, 4 bits wide
  Subtractor #(.width(4)) subtractor_1 (
    .a(bit_extender_2_out), .b(4'b0001), .out(subtractor_1_out));  // open: bin, bout
  Comparator #(.width(4)) comparator_1 (.a(bit_extender_2_out), .b(4'b0000), .eq(comparator_1_eq));  // open: gt, lt
  Comparator #(.width(16)) comparator_2 (.a(Z), .b({16{1'b0}}), .eq(comparator_2_eq));  // open: gt, lt
  assign Z_2 = not_2_out ? comparator_2_eq : 1'bz;  // Controlled_Buffer controlled_buffer_20
  not not_2 (not_2_out, nop);
  xor xor_3 (xor_3_out, Z[15], X[15]);
  and and_2 (and_2_out, xor_3_out, xnor_1_out);
  xnor xnor_1 (xnor_1_out, X[15], xor_1_out[15]);
  BitSelector #(.width(16)) bitselector_1 (.in(X), .out(bitselector_1_out), .sel(not_1_out));
  assign controlled_buffer_21_out = shl ? bitselector_1_out : 1'bz;  // Controlled_Buffer controlled_buffer_21
  assign controlled_buffer_21_out = or_2_out ? bitselector_2_out : 1'bz;  // Controlled_Buffer controlled_buffer_22
  BitSelector #(.width(16)) bitselector_2 (.in(X), .out(bitselector_2_out), .sel(subtractor_1_out));
  or or_2 (or_2_out, shr, sar);
  not not_3 (not_3_out, comparator_1_eq);
  assign S = tunnel ? Z[15] : 1'bz;  // Controlled_Buffer controlled_buffer_23
  assign O = tunnel ? and_2_out : 1'bz;  // Controlled_Buffer controlled_buffer_24
  assign C = not_3_out ? controlled_buffer_21_out : 1'bz;  // Controlled_Buffer controlled_buffer_25
  Decoder #(.select(4), .disabled(0), .enable("false")) decoder_1 (
    .out0(nop), .out1(X_t), .out2(Y_t), .out3(tunnel), .out4(mul), .out5(div), .out6(\and ), .out7(\or ),
    .out8(\nand ), .out9(\nor ), .out10(\xor ), .out11(shl), .out12(shr), .out13(sar), .out14(rol),
    .out15(ror), .sel(instr));

  // Notes on the sheet:
  //   extra bits for mul or div
  //   mul: carry in
  //   div: upper half of divisor
  //   A rotation by a multiple of 16
  //   bits does nothing. For shifts
  //   the logic isn't as clear but
  //   either way we ignore the
  //   upper 12 bits of Y to get a
  //   4 bit
  //   number between 0 and 15
  //   for the shift/rotation distance
  //   LL
  //   LR
  //   AR
  //   RL
  //   RR
  //   check most significant bits
  //   to detect overflow
  //   zero
  //   set Zero flag, except when no
  //   operation was performed
  //   instruction decoding:
  //   sign
  //   set S and O flags
  //   only with + operation
  //   overflow
  //   carry
  //   extra bits for mul or div
  //   mul: upper half of result aka carry out
  //   div: remainder
  //   for shifts, the carry bit is the last bit
  //   that was shifted out of the register.
  //   We disable setting the carry bit for
  //   shifts by zero places, because in that
  //   case no bit gets shifted out.
  //   Since we are using logisim's built-ins
  //   for bit shifts, we use "select" elements
  //   to select the (n-1)th bit in X, or the
  //   (16-(n-1))th bit for left shifts.
endmodule

module decoder (
  input  [15:0] instr,
  input  [1:0] phase,
  input  [3:0] flags,
  output RSTPhase,
  output [1:0] pcsel,
  output pcload,
  output loadir,
  output HLT,
  output datsel,
  output memwr,
  output [1:0] adrsel,
  output [1:0] regsel,
  output loadim,
  output regwr,
  output [2:0] Ysel,
  output [2:0] Zsel,
  output [2:0] Xsel,
  output [3:0] ALUop,
  output XXen,
  output cin,
  output ZZwr,
  output invY,
  output Yenable
);

  wire and_1_out, and_6_out, and_7_out, and_8_out, and_12_out, and_14_out, CALL, CALL_plus, CALLR,
       comparator_2_eq, comparator_3_eq, comparator_4_eq, comparator_5_eq, comparator_6_lt, comparator_7_eq,
       DIVC, DIVD, eq7_1_out_3, eq7_2_out_3, eq7_3_out_3, eq7_4_out_3, eq7_5_out_3, eq7_6_out_3, eq7_7_out_3,
       imm, MULC, multiplexer_3_out, multiplexer_14_out, nor_1_out, nor_4_out, not_1_out, not_2_out,
       not_3_out, not_5_out, not_6_out, or_1_out, or_2_out, or_3_out, or_4_out, or_7_out, or_8_out,
       or_12_out, or_13_out, ph_1, ph_2, ph_3, POP, PUSH, REM, RET, STO_imm, STO_reg, xor_1_out;
  wire [0:0] nand_1_out;
  wire [1:0] multiplexer_9_out, multiplexer_10_out, multiplexer_13_out, nor_3_out, or_14_out;
  wire [3:0] _0011xxx_ALUop, _0101xxx_ALUop, _0110xxx_ALUop, bit_extender_1_out, multiplexer_12_out,
       multiplexer_15_out;

  xor xor_1 (xor_1_out, flags[1], flags[0]);
  not not_1 (not_1_out, xor_1_out);
  Multiplexer #(.width(3), .enable("false")) multiplexer_1 (
    .in0(instr[2:0]), .in1(3'b111), .out(Ysel), .sel(and_1_out));
  and and_1 (and_1_out, ph_2, or_1_out);
  or or_1 (or_1_out, POP, CALL_plus, RET);
  Multiplexer #(.select(3), .width(4), .enable("false")) multiplexer_2 (
    .in0(4'b0101), .in1(4'b0100), .in2(4'b0101), .in3(4'b0101), .in4(4'b0100), .in5(4'b0101), .in6(4'b0000),
    .in7(4'b0000), .out(_0101xxx_ALUop), .sel(instr[11:9]));
  Comparator #(.width(7)) comparator_1 (.a(7'b1111011), .b(instr[15:9]), .eq(POP));  // open: gt, lt
  not not_2 (not_2_out, flags[3]);
  not not_3 (not_3_out, flags[2]);
  nor nor_1 (nor_1_out, instr[9], instr[10], instr[11]);
  Adder #(.width(4)) adder_1 (.a(4'b1011), .b(bit_extender_1_out), .out(_0110xxx_ALUop));  // open: cin, cout
  assign bit_extender_1_out = {{1{1'b0}}, instr[11:9]};  // Bit_Extender bit_extender_1
  Comparator #(.width(6), .mode("unsigned")) comparator_2 (
    .a({instr[15:11], instr[9]}), .b(6'b010000), .eq(comparator_2_eq));  // open: gt, lt
  eq7 eq7_1 (.A(instr[15:9]), .B(7'b0011001), .out_3(eq7_1_out_3));
  eq7 eq7_2 (.A(instr[15:9]), .B(7'b0011111), .out_3(eq7_2_out_3));
  eq7 eq7_3 (.A(instr[15:9]), .B(7'b0010011), .out_3(eq7_3_out_3));
  eq7 eq7_4 (.A(instr[15:9]), .B(7'b0100001), .out_3(eq7_4_out_3));
  eq7 eq7_5 (.A(instr[15:9]), .B(7'b0100010), .out_3(eq7_5_out_3));
  eq7 eq7_6 (.A(instr[15:9]), .B(7'b0100011), .out_3(eq7_6_out_3));
  Comparator #(.width(6), .mode("unsigned")) comparator_3 (
    .a(instr[15:10]), .b(6'b001001), .eq(comparator_3_eq));  // open: gt, lt
  eq7 eq7_7 (.A(instr[15:9]), .B(7'b0010100), .out_3(eq7_7_out_3));
  Comparator #(.width(6), .mode("unsigned")) comparator_4 (
    .a(instr[15:10]), .b(6'b010000), .eq(comparator_4_eq));  // open: gt, lt
  or or_2 (or_2_out, POP, CALLR);
  nand nand_1 (nand_1_out[0], instr[12], ~instr[13], instr[14], instr[15]);  // NAND_Gate
  Multiplexer #(.select(3), .enable("false")) multiplexer_3 (
    .in0(1'b1), .in1(flags[3]), .in2(not_2_out), .in3(not_1_out), .in4(xor_1_out), .in5(not_3_out),
    .in6(flags[2]), .in7(1'b0), .out(multiplexer_3_out), .sel(instr[11:9]));
  nor nor_2 (loadir, phase[0], phase[1]);
  or or_3 (or_3_out, PUSH, CALL_plus, RET, ph_3);
  and and_2 (ph_1, phase[0], ~phase[1]);  // AND_Gate
  and and_3 (ph_2, ~phase[0], phase[1]);  // AND_Gate
  and and_4 (ph_3, phase[0], phase[1]);
  and and_5 (RSTPhase, ~or_2_out, ph_3);  // AND_Gate
  and and_6 (and_6_out, ~instr[10], instr[12], instr[13], instr[14], instr[15]);  // AND_Gate
  not not_4 (datsel, instr[15]);
  or or_4 (or_4_out, STO_imm, STO_reg, PUSH, CALLR, CALL);
  or or_5 (CALL_plus, CALL, CALLR);
  or or_6 (nor_3_out[1], ~instr[12], instr[13], instr[14], instr[15]);  // OR_Gate
  nor nor_3 (nor_3_out[0], STO_reg, PUSH, CALL_plus);
  Multiplexer #(.select(4), .enable("false")) multiplexer_4 (
    .in0(1'b0), .in1(1'b1), .in2(1'b0), .in3(1'b0), .in4(1'b0), .in5(1'b0), .in6(1'b0), .in7(1'b0),
    .in8(1'b0), .in9(1'b0), .in10(1'b0), .in11(1'b0), .in12(1'b1), .in13(1'b0), .in14(1'b0),
    .in15(nor_1_out), .out(imm), .sel(instr[15:12]));
  Multiplexer #(.width(3), .enable("false")) multiplexer_5 (.in0(instr[8:6]), .in1(3'b111), .out(Zsel), .sel(or_3_out));
  Multiplexer #(.select(3), .width(4), .enable("false")) multiplexer_6 (
    .in0(4'b0011), .in1(4'b0011), .in2(4'b0110), .in3(4'b0111), .in4(4'b1000), .in5(4'b1001), .in6(4'b1010),
    .in7(4'b0011), .out(_0011xxx_ALUop), .sel(instr[11:9]));
  and and_7 (and_7_out, POP, ph_3);
  or or_7 (or_7_out, eq7_1_out_3, eq7_2_out_3, eq7_3_out_3, eq7_4_out_3, eq7_5_out_3, eq7_6_out_3, CALL_plus);
  nor nor_4 (nor_4_out, CALL_plus, comparator_3_eq, eq7_7_out_3, comparator_4_eq, POP);
  Multiplexer #(.select(2), .width(2), .enable("false")) multiplexer_7 (
    .in0(2'b10), .in1(2'b10), .in2({RET, nand_1_out[0]}), .in3(2'b00), .out(pcsel), .sel(phase));
  and and_8 (and_8_out, ~instr[13], instr[14], instr[15], multiplexer_3_out);  // AND_Gate
  or or_8 (or_8_out, and_8_out, and_6_out);
  assign adrsel = nor_3_out & {2{ph_2}};  // AND_Gate and_9, 2 bits wide
  and and_10 (loadim, imm, ph_1);
  or or_9 (cin, and_7_out, RET, comparator_2_eq, eq7_1_out_3, eq7_2_out_3);
  and and_11 (invY, or_7_out, ~ph_3);  // AND_Gate
  and and_12 (and_12_out, CALLR, ph_3);
  or or_10 (Yenable, and_12_out, nor_4_out);
  and and_13 (memwr, ph_2, or_4_out);
  Multiplexer #(.select(2), .enable("false")) multiplexer_8 (
    .in0(1'b1), .in1(imm), .in2(or_8_out), .in3(CALLR), .out(pcload), .sel(phase));
  Multiplexer #(.select(3), .width(2), .enable("false")) multiplexer_9 (
    .in0(2'b00), .in1(2'b01), .in2(2'b01), .in3(2'b10), .in4(2'b10), .in5(2'b10), .in6(2'b10), .in7(2'b10),
    .out(multiplexer_9_out), .sel(instr[11:9]));
  or or_11 (or_14_out[1], PUSH, CALL_plus, POP);
  Comparator #(.width(7)) comparator_5 (.a(instr[15:9]), .b(7'b0000001), .eq(comparator_5_eq));  // open: gt, lt
  Comparator #(.width(4), .mode("unsigned")) comparator_6 (
    .a(instr[15:12]), .b(4'b0011), .lt(comparator_6_lt));  // open: gt, eq
  Multiplexer #(.width(2), .enable("false")) multiplexer_10 (
    .in0(2'b10), .in1(multiplexer_9_out), .out(multiplexer_10_out), .sel(comparator_6_lt));
  not not_5 (not_5_out, instr[10]);
  or or_12 (or_12_out, instr[9], ~instr[10], instr[11]);  // OR_Gate
  not not_6 (not_6_out, and_14_out);
  and and_14 (and_14_out, instr[9], instr[10], instr[11]);
  or or_13 (or_13_out, instr[11], instr[10], instr[11]);
  Multiplexer #(.select(2), .width(3), .enable("false")) multiplexer_11 (
    .in0(instr[5:3]), .in2(3'b111), .out(Xsel), .sel(or_14_out));  // open: in1, in3
  or or_14 (or_14_out[0], comparator_7_eq, RET);
  Comparator #(.width(6), .mode("unsigned")) comparator_7 (
    .a(instr[15:10]), .b(6'b010001), .eq(comparator_7_eq));  // open: gt, lt
  Multiplexer #(.select(4), .width(4), .enable("false")) multiplexer_12 (
    .in0(4'b0000), .in1(4'b0000), .in2(4'b0011), .in3(_0011xxx_ALUop), .in4(4'b0011), .in5(_0101xxx_ALUop),
    .in6(_0110xxx_ALUop), .in7(4'b0000), .in8(4'b0000), .in9(4'b0000), .in10(4'b0000), .in11(4'b0000),
    .in12(4'b0000), .in13(4'b0010), .in14(4'b0011), .in15(4'b0011), .out(multiplexer_12_out),
    .sel(instr[15:12]));
  eq7 eq7_8 (.A(instr[15:9]), .B(7'b0001010), .out_3(STO_imm));
  eq7 eq7_9 (.A(instr[15:9]), .B(7'b0010010), .out_3(STO_reg));
  eq7 eq7_10 (.A(instr[15:9]), .B(7'b0010011), .out_3(PUSH));
  eq7 eq7_11 (.A(instr[15:9]), .B(7'b1111000), .out_3(CALL));
  eq7 eq7_12 (.A(instr[15:9]), .B(7'b1111010), .out_3(CALLR));
  eq7 eq7_13 (.A(instr[15:9]), .B(7'b1111001), .out_3(RET));
  eq7 eq7_14 (.A(instr[15:9]), .B(7'b0101000), .out_3(REM));
  eq7 eq7_15 (.A(instr[15:9]), .B(7'b0101001), .out_3(MULC));
  eq7 eq7_16 (.A(instr[15:9]), .B(7'b0101010), .out_3(DIVD));
  eq7 eq7_17 (.A(instr[15:9]), .B(7'b0101011), .out_3(DIVC));
  Multiplexer #(.width(2), .enable("false")) multiplexer_13 (
    .in0(multiplexer_10_out), .in1(2'b01), .out(multiplexer_13_out), .sel(POP));
  Multiplexer #(.select(4), .enable("false")) multiplexer_14 (
    .in0(1'b0), .in1(not_5_out), .in2(or_12_out), .in3(not_6_out), .in4(1'b1), .in5(or_13_out), .in6(1'b1),
    .in7(1'b0), .in8(1'b0), .in9(1'b0), .in10(1'b0), .in11(1'b0), .in12(1'b0), .in13(1'b0), .in14(1'b0),
    .in15(1'b1), .out(multiplexer_14_out), .sel(instr[15:12]));
  Multiplexer #(.width(4), .enable("false")) multiplexer_15 (
    .in0(4'b0010), .in1(4'b0011), .out(multiplexer_15_out), .sel(POP));
  or or_15 (XXen, REM, MULC, DIVD, DIVC);
  or or_16 (ZZwr, REM, MULC, DIVC);
  and and_15 (HLT, comparator_5_eq, phase[1]);
  Multiplexer #(.select(2), .width(2), .enable("false")) multiplexer_16 (
    .in0(2'b00), .in1(2'b00), .in2(multiplexer_13_out), .in3(2'b10), .out(regsel), .sel(phase));
  Multiplexer #(.select(2), .enable("false")) multiplexer_17 (
    .in0(1'b0), .in1(1'b0), .in2(multiplexer_14_out), .in3(POP), .out(regwr), .sel(phase));
  Multiplexer #(.select(2), .width(4), .enable("false")) multiplexer_18 (
    .in0(4'b0000), .in1(4'b0000), .in2(multiplexer_12_out), .in3(multiplexer_15_out), .out(ALUop), .sel(phase));

  // Other names for the same wires on the sheet: O = flags[0]; S = flags[1]; C = flags[2]; Z = flags[3];
  //   Ysel_t[2:0] = instr[2:0]; Xsel_t[2:0] = instr[5:3]; Zsel_t[2:0] = instr[8:6]; op0_2[2:0] = instr[11:9];
  //   opcode[6:0] = instr[15:9]; op3_6[3:0] = instr[15:12]; ph0 = phase[0]; ph1 = phase[1]

  // Notes on the sheet:
  //   Select new PC source
  //   Update program counter
  //   Load instruction
  //   Select data out
  //   Write to memory
  //   Select memory address
  //   Load immediate value
  //   Register selection
  //   Arithmetic and Logic Unit (ALU) - operations
  //   Arithmetic and Logic Unit (ALU) - extra control flags
  //   PUSH
  //   DEC
  //   NEG
  //   INV
  //   MOV (btw registers)
  //   Execution Phase Control
  //   INC
  //   NEG
  //   SUB
  //   CMP
  //   STO [src2]
  //   PUSH
  //   INC
  //   DEC
  //   Program Counter
  //   Data Flow
  //   multiplication and division
  //   ---------------
  //   /\
  //   Conditional jumps
  //   bit shifts
  //   check for a "jump to address in register" instruction code
  //   (op3-6 = "1101" little-endian)
  //   only if 110xxxx or 1111xxx
  //   simple operations
  //   (+, -, binary logic operators)
  //   Instruction decoding
  //   STO [imm]
  //   STO [reg]
  //   PUSH
  //   CALL
  //   CALL reg
  //   MULC
  //   HALT instruction
  //   Resgister file writing
  //   RET
  //   REM
  //   DIVD
  //   DIVC
  //   ALU flags
  //   RET, NEG and INV
  //   X input must be disconnected
endmodule

module incr16 (
  input  [15:0] IN,
  output [15:0] OUT,
  output carry
);

  Adder #(.width(16)) adder_1 (.a(IN), .b({16{1'b0}}), .out(OUT), .cin(1'b1), .cout(carry));
endmodule

module eq7 (
  input  [6:0] A,
  input  [6:0] B,
  output out_3
);

  Comparator #(.width(7), .mode("unsigned")) comparator_1 (.a(A), .b(B), .eq(out_3));  // open: gt, lt
endmodule

module eq16 (
  input  [15:0] A,
  input  [15:0] B,
  output out_3
);

  Comparator #(.width(16), .mode("unsigned")) comparator_1 (.a(A), .b(B), .eq(out_3));  // open: gt, lt
endmodule

module flags_reg (
  input  Z,
  input  C,
  input  S,
  input  O,
  input  clk,
  input  rst,
  output [3:0] Q
);

  Register #(.width(1)) register_1 (.D(Z), .Q(Q[3]), .clk(clk), .clr(rst));  // open: en
  Register #(.width(1)) register_2 (.D(C), .Q(Q[2]), .clk(clk), .clr(rst));  // open: en
  Register #(.width(1)) register_3 (.D(S), .Q(Q[1]), .clk(clk), .clr(rst));  // open: en
  Register #(.width(1)) register_4 (.D(O), .Q(Q[0]), .clk(clk), .clr(rst));  // open: en
endmodule
